// Digital circuit ComputerDisplayKeyboard.dig as structural Verilog
module ComputerDisplayKeyboard (
  input  reset,
  input  C
);

  wire _1_2_out, _1_out, _2_out, _3_out, _4_out, CPU_p7, demultiplexer_1_out_0, demultiplexer_1_out_1,
       demultiplexer_1_out_2, or_1_out;
  wire [14:0] CPU_p5, CPU_p8;
  wire [15:0] CPU_p1, CPU_p6, hackdisplay_1_p6, KbdController_out, Program_d, ramdualport_1_d;

  ROM #(.AddrBits(15), .Bits(16)) Program (.A(CPU_p8), .sel(1'b1), .D(Program_d));
  // CPU CPU: pin names not known; wires that end beside it: CPU_p1, reset, Program_d, C, CPU_p5, CPU_p6, CPU_p7, CPU_p8
  Demultiplexer #(.Selector_Bits(2)) demultiplexer_1 (
    .sel(CPU_p5[14:13]), .in(CPU_p7), .out_0(demultiplexer_1_out_0), .out_1(demultiplexer_1_out_1),
    .out_2(demultiplexer_1_out_2));  // open: out_3
  or or_1 (or_1_out, demultiplexer_1_out_0, demultiplexer_1_out_1);
  Button _1 (.out(_1_out));
  Button _2 (.out(_2_out));
  Button _3 (.out(_3_out));
  Button _4 (.out(_4_out));
  RAMDualPort #(.AddrBits(15), .Bits(16)) ramdualport_1 (
    .A(CPU_p5), .Din(CPU_p6), .str(or_1_out), .C(C), .ld(1'b1), .D(ramdualport_1_d));
  // HackDisplay hackdisplay_1: pin names not known; wires that end beside it: CPU_p5[12:0], CPU_p6, demultiplexer_1_out_2, C, 1'b1, hackdisplay_1_p6
  Multiplexer #(.Bits(16)) multiplexer_1 (.sel(_1_2_out), .in_0(16'h31), .in_1({16{1'b0}}));  // open: out
  Button #(.activeLow("true")) _1_2 (.out(_1_2_out));
  LookUpTable #(.Bits(16)) KbdController (
    .in0(_1_out), .in1(_2_out), .in2(_3_out), .in3(_4_out), .out(KbdController_out));
  Multiplexer #(.Selector_Bits(2), .Bits(16)) multiplexer_2 (
    .sel(CPU_p5[14:13]), .in_0(ramdualport_1_d), .in_1(ramdualport_1_d), .in_2(hackdisplay_1_p6),
    .in_3(KbdController_out), .out(CPU_p1));

  // Notes on the sheet:
  //   C: Hz: 2147483647
  //   contents of Program (hex, n*v repeats v):
  //   2,ec10,3,e090,0,e308
  //   contents of KbdController (hex, n*v repeats v):
  //   0,31,32,0,33,0,0,0,34
endmodule
