// Digital circuit ComputerFull4Key.dig as structural Verilog
module ComputerFull4Key (
  input  reset,
  input  C
);

  wire _1_out, _2_out, _3_out, _4_out, CPU_p1;
  wire [14:0] CPU_p8;
  wire [15:0] CPU_p5, CPU_p6, CPU_p7, Program_d;

  ROM #(.AddrBits(15), .Bits(16)) Program (.A(CPU_p8), .sel(1'b1), .D(Program_d));
  // CPU CPU: pin names not known; wires that end beside it: CPU_p1, reset, Program_d, C, CPU_p5, CPU_p6, CPU_p7, CPU_p8
  Button _1 (.out(_1_out));
  Button _2 (.out(_2_out));
  Button _3 (.out(_3_out));
  Button _4 (.out(_4_out));
  Memory memory_1 (
    .C(C), .add(CPU_p5), .outM(CPU_p6), .load(CPU_p7), .key1(_1_out), .key2(_2_out), .key3(_3_out),
    .key4(_4_out), .out(CPU_p1));

  // Notes on the sheet:
  //   C: Hz: 2147483647
  //   contents of Program (hex, n*v repeats v):
  //   2,ec10,3,e090,0,e308
endmodule
