// Digital circuit Memory.dig as structural Verilog
module Memory (
  input  C,
  input  [15:0] add,
  input  [15:0] outM,
  input  [15:0] load,
  input  key1,
  input  key2,
  input  key3,
  input  key4,
  output [15:0] out
);

  wire demultiplexer_1_out_0, demultiplexer_1_out_1, demultiplexer_1_out_2, or_1_out;
  wire [15:0] hackdisplay_1_p6, KbdController_out, ramdualport_1_d;

  Demultiplexer #(.Selector_Bits(2)) demultiplexer_1 (
    .sel(add[14:13]), .in(load[0]), .out_0(demultiplexer_1_out_0), .out_1(demultiplexer_1_out_1),
    .out_2(demultiplexer_1_out_2));  // open: out_3
  or or_1 (or_1_out, demultiplexer_1_out_0, demultiplexer_1_out_1);
  RAMDualPort #(.AddrBits(15), .Bits(16)) ramdualport_1 (
    .A(add[14:0]), .Din(outM), .str(or_1_out), .C(C), .ld(1'b1), .D(ramdualport_1_d));
  // HackDisplay hackdisplay_1: pin names not known; wires that end beside it: add[12:0], outM, demultiplexer_1_out_2, C, 1'b1, hackdisplay_1_p6
  LookUpTable #(.Bits(16)) KbdController (.in0(key1), .in1(key2), .in2(key3), .in3(key4), .out(KbdController_out));
  Multiplexer #(.Selector_Bits(2), .Bits(16)) multiplexer_1 (
    .sel(add[14:13]), .in_0(ramdualport_1_d), .in_1(ramdualport_1_d), .in_2(hackdisplay_1_p6),
    .in_3(KbdController_out), .out(out));
  // Pins of 1 and 16 bits meet at out
  // Pins of 1 and 16 bits meet at load
  // Pins of 15 and 16 bits meet at add

  // Notes on the sheet:
  //   C: Hz: 2147483647
  //   add: Memory Address
  //   outM: ALU output
  //   load: Write Signal
  //   out: Memory output
  //   contents of KbdController (hex, n*v repeats v):
  //   0,31,32,0,33,0,0,0,34
endmodule
